// Logisim project neslogisim.circ as structural Verilog: 2 circuits, main circuit main
module main (
);

  wire clock_1_out, midi2freq_1_enable, midi2freq_2_enable, midi2freq_3_enable, midi2freq_4_enable;
  wire [13:0] midi2freq_1_freq, midi2freq_2_freq, midi2freq_3_freq, midi2freq_4_freq;
  wire [15:0] counter_1_q;
  wire [31:0] rom_1_data;

  Clock clock_1 (.out(clock_1_out));
  Counter #(.max('hffff), .width(16)) counter_1 (
    .clk(clock_1_out), .Q(counter_1_q));  // open: clr, load, up, count, D, carry
  ROM #(.addrWidth(16), .dataWidth(32)) rom_1 (.addr(counter_1_q), .data(rom_1_data));
  midi2freq midi2freq_1 (.Enable(midi2freq_1_enable), .Freq(midi2freq_1_freq), .MIDI(rom_1_data[7:0]));
  midi2freq midi2freq_2 (.Enable(midi2freq_2_enable), .Freq(midi2freq_2_freq), .MIDI(rom_1_data[15:8]));
  midi2freq midi2freq_3 (.Enable(midi2freq_3_enable), .Freq(midi2freq_3_freq), .MIDI(rom_1_data[23:16]));
  midi2freq midi2freq_4 (.Enable(midi2freq_4_enable), .Freq(midi2freq_4_freq), .MIDI(rom_1_data[31:24]));
  // Buzzer #(.smooth_level(1), .smooth_width(1), .waveform("Square")) buzzer_1: pin names not known; wires that end beside it: midi2freq_1_freq, midi2freq_1_enable, {7{1'b1}}, 8'h24
  // Buzzer #(.smooth_level(1), .waveform("Square")) buzzer_2: pin names not known; wires that end beside it: midi2freq_2_freq, midi2freq_2_enable, {7{1'b1}}, 8'h29
  // Buzzer #(.smooth_level(0), .waveform("Triangle")) buzzer_3: pin names not known; wires that end beside it: midi2freq_3_freq, midi2freq_3_enable, {7{1'b1}}
  // Buzzer #(.smooth_level(0), .waveform("Noise")) buzzer_4: pin names not known; wires that end beside it: midi2freq_4_freq, midi2freq_4_enable, {7{1'b1}}

  // Notes on the sheet:
  //   contents of rom_1 (hex, n*v repeats v):
  //   0 6*becfc7 6*bdcec6 6*0 6*bccdc5 6*bbcac1 6*0 6*b7c7be 6*b5c5bc 6*0 6*b4c4bb bcb2c3bb 8*b2c3bb 9*0
  //   bcbecfc7 5*becfc7 bcbecfc7 becfc7 becfc7 0 0 0 bc000000 5*0 bcb2c3c1 8*b2c3c1 c3c1 c3c1 c3c1
  //   bc00c3c1 5*c3c1 bcb70000 5*b70000 bcb70000 b70000 b70000 0 0 0 bc000000 5*0 6*b0cfc8 b00000 b00000
  //   b00000 0 0 0 6*c8c0 bcb7ccc3 5*b7ccc3 b70000 b70000 b70000 0 0 0 6*cfc8 9*b0cfc8 cfc8 cfc8 cfc8
  //   6*c8c0 bcb7ccc3 5*b7ccc3 b70000 b70000 b70000 0 0 0 6*cfc8 6*afc7bf afcbc3 afcbc3 afcbc3 cbc3 cbc3
  //   cbc3 6*cfc7 bcb7d3cb 5*b7d3cb b70000 b70000 b70000 0 0 0 6*d1c7 bcafd1c7 5*afd1c7 bcafd1c7 afd1c7
  //   afd1c7 d1c7 d1c7 d1c7 bc00d1c7 5*d1c7 bcb7d1c7 8*b7d1c7 d1c7 d1c7 d1c7 bc000000 5*0 6*aecfc6 ae0000
  //   ae0000 ae0000 0 0 0 6*c6be bcb7cac3 5*b7cac3 b70000 b70000 b70000 0 0 0 6*cfc6 9*aecfc6 cfc6 cfc6
  //   cfc6 6*c6be bcb7cac3 5*b7cac3 b70000 b70000 b70000 0 0 0 6*cfc6 6*adc9c0 adccc5 adccc5 adccc5 ccc5
  //   ccc5 ccc5 6*cfc9 bcb7d3cc 5*b7d3cc b70000 b70000 b70000 0 0 0 6*d1c9 bcadd1c9 5*add1c9 bcadd1c9
  //   add1c9 add1c9 d1c9 d1c9 d1c9 bc00d1c9 5*d1c9 bcb7d1c9 8*b7d1c9 d1c9 d1c9 d1c9 bc00d3cc 5*d3cc
  //   6*a9d4d1 a90000 a90000 a90000 0 0 0 6*d3cf bcb5d4d1 5*b5d4d1 b50000 b50000 b50000 0 0 0 6*d1cd
  //   9*aad1cd d1cd d1cd d1cd 6*d4d1 bcb6d3cf 5*b6d3cf b60000 b60000 b60000 0 0 0 6*d1ce 6*abcfcc ab0000
  //   ab0000 ab0000 0 0 0 6*cecb bcb7cfcc 5*b7cfcc b70000 b70000 b70000 0 0 0 6*ccc8 bcadccc8 5*adccc8
  //   bcadccc8 adccc8 adccc8 ccc8 ccc8 ccc8 bc00c9c5 5*c9c5 bcb9cac7 5*b9cac7 b90000 b90000 b90000 0 0 0
  //   bc00ccc9 5*ccc9 6*b2cdca b20000 b20000 b20000 0 0 0 6*ccc8 bcb5cdca 5*b5cdca b50000 b50000 b50000 0
  //   0 0 6*c7c3 9*abc7c3 c7c3 c7c3 c7c3 6*ccc8 bcb2cac7 5*b2cac7 b20000 b20000 b20000 0 0 0 6*c8c3
  //   9*b0c8c3 9*c8c3 bcabc8c3 8*abc8c3 c8c3 c8c3 c8c3 6*0 bcb00000 5*b00000 bcb00000 b00000 b00000 0 0 0
  //   bc000000 5*0 bc000000 11*0 bc000000 5*0 5*bcb0c8c3 4*b0c8c3 c8c3 c8c3 c8c3 6*ccc3 bcb2ccc3 8*b2ccc3
  //   ccc3 ccc3 ccc3 bc00ccc3 5*ccc3 5*bcb4cfc8 4*b4cfc8 9*cfc8 bcb7d1cc 8*b7d1cc d1cc d1cc d1cc bc00d4cf
  //   5*d4cf 5*bcb9d4cf 4*b9d4cf 9*d4cf bcb7d4cf 8*b7d4cf d4cf d4cf d4cf bc00d4cf 5*d4cf 5*bcb4d1cc
  //   4*b4d1cc d1cc d1cc d1cc 6*cfc8 bcb0ccc5 8*b0ccc5 ccc5 ccc5 ccc5 bc00c8c3 5*c8c3 5*bcb2cac2 4*b2cac2
  //   cac2 cac2 cac2 6*ccc3 bcb4cac2 8*b4cac2 cac2 cac2 cac2 bc00ccc3 5*ccc3 5*bcb6cac2 4*b6cac2 cac2 cac2
  //   cac2 6*c5be bcadc5be 8*adc5be c5be c5be c5be bc00cac2 5*cac2 5*bcb2cac2 b2cac2 6*cac2 4*b4c5be
  //   b4cac2 b4cac2 bcb0cac2 b0cac2 4*b0c5be b0cabe b0cabe b0cabe cabe c5c2 c5c2 bc00c5c2 c5c2 4*cabe
  //   4*bcafc5c2 bcafcabe afcabe afcabe afcabe afc5c2 c5c2 c5c2 c5c2 4*cabe c5c2 c5c2 bcadc5c2 adc5c2
  //   7*adcabe cabe cabe cabe bc00cac1 5*cac1 5*bcabcac1 4*abcac1 cac1 cac1 cac1 6*ccc3 bcb7cac1 8*b7cac1
  //   cac1 cac1 cac1 bc00ccc3 5*ccc3 5*bcb5cac1 4*b5cac1 cac1 cac1 cac1 6*ccc3 bcb2ccc3 8*b2ccc3 ccc3 ccc3
  //   ccc3 bc00d1c8 5*d1c8 5*bcafd1c8 4*afd1c8 d1c8 d1c8 d1c8 6*cfc7 bcabd1c8 8*abd1c8 d1c8 d1c8 d1c8
  //   bc00cfc7 5*cfc7 5*bcadccc3 4*adccc3 ccc3 ccc3 ccc3 6*cac1 bcafc8c0 8*afc8c0 c8c0 c8c0 c8c0 bc00ccc8
  //   5*ccc8 5*bcb0ccc8 4*b0ccc8 ccc8 ccc8 ccc8 4*c3c0 ccc8 ccc8 bcb1ccc8 b1ccc8 4*b1c3c0 b1ccc8 b1ccc8
  //   b1ccc8 ccc8 c3c0 c3c0 bc00c3c0 c3c0 4*ccc8 4*bcb2c3c0 bcb2ccc8 b2ccc8 b2ccc8 b2ccc8 b2c3c0 c3c0 c3c0
  //   c3c0 4*ccc8 c3c0 c3c0 bcb3c3c0 b3c3c0 7*b3ccc8 ccc8 ccc8 ccc8 bc00ccc8 5*ccc8 5*bcb4ccc8 b4ccc8
  //   6*ccc8 6*afcfc7 bcadcfc7 5*adcfc7 adcbc5 adcbc5 adcbc5 cbc5 cbc5 cbc5 bc00cbc5 5*cbc5 5*bcabc7c3
  //   4*abc7c3 c7c3 c7c3 c7c3 6*c5c1 bcafc5c1 5*afc5c1 afc3bf afc3bf afc3bf c3bf c3bf c3bf bc00c3bf 5*c3bf
  //   5*bcb0c3bf 4*b0c3bf c3bf c3bf c3bf 6*ccc3 bcb2ccc3 8*b2ccc3 ccc3 ccc3 ccc3 bc00ccc3 5*ccc3
  //   5*bcb4cfc8 4*b4cfc8 9*cfc8 bcb7d1cc 8*b7d1cc d1cc d1cc d1cc bc00d4cf 5*d4cf 5*bcb9d4cf 4*b9d4cf
  //   9*d4cf bcb7d4cf 8*b7d4cf d4cf d4cf d4cf bc00d4cf 5*d4cf 5*bcb4d1cc 4*b4d1cc d1cc d1cc d1cc 6*cfc8
  //   bcb0ccc5 8*b0ccc5 ccc5 ccc5 ccc5 bc00c8c3 5*c8c3 5*bcb2cac2 4*b2cac2 cac2 cac2 cac2 6*ccc3 bcb4cac2
  //   8*b4cac2 cac2 cac2 cac2 bc00ccc3 5*ccc3 5*bcb6cac2 4*b6cac2 cac2 cac2 cac2 6*c5be bcadc5be 8*adc5be
  //   c5be c5be c5be bc00cac2 5*cac2 5*bcb2cac2 b2cac2 6*cac2 4*b4c5be b4cac2 b4cac2 bcb0cac2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
endmodule

module midi2freq (
  input  [7:0] MIDI,
  output Enable,
  output [13:0] Freq
);

  ROM #(.addrWidth(7), .dataWidth(14)) rom_1 (.addr(MIDI[6:0]), .data(Freq));

  assign Enable = MIDI[7];

  // Notes on the sheet:
  //   contents of rom_1 (hex, n*v repeats v):
  //   8 9 9 a a b c c d e f f 10 11 12 13 15 16 17 18 1a 1c 1d 1f 21 23 25 27 29 2c 2e 31 34 37 3a 3e 41
  //   45 49 4e 52 57 5c 62 68 6e 75 7b 83 8b 93 9c a5 af b9 c4 d0 dc e9 f7 106 115 126 137 14a 15d 172 188
  //   19f 1b8 1d2 1ee 20b 22a 24b 26e 293 2ba 2e4 310 33f 370 3a4 3dc 417 455 497 4dd 527 575 5c8 620 67d
  //   6e0 749 7b8 82d 8a9 92d 9b9 a4d aea b90 c40 cfa dc0 e91 f6f 105a 1153 125b 1372 149a 15d4 1720 1880
  //   19f5 1b80 1d23 1ede 20b4 22a6 24b5 26e4 2934 2ba7 2e40 3100
endmodule
